// Logisim project lab2.3a.circ as structural Verilog: 1 circuit, main circuit main
module main (
  input  A,
  input  B,
  input  C,
  input  A_2,
  input  B_2,
  input  C_2
);

  wire nand_1_out, nand_2_out, nand_3_out, nand_4_out, nand_5_out, nand_6_out, nand_7_out, nand_8_out,
       nand_9_out, nand_10_out, nand_11_out, nand_12_out, not_1_out, not_2_out, not_3_out, not_4_out,
       not_5_out, not_6_out, not_7_out, not_8_out, not_9_out, not_10_out, not_11_out, not_12_out, not_13_out,
       not_14_out, not_15_out, not_16_out, not_17_out, not_18_out;

  not not_1 (not_1_out, B);
  not not_2 (not_2_out, A);
  not not_3 (not_3_out, A);
  not not_4 (not_4_out, B_2);
  not not_5 (not_5_out, A_2);
  not not_6 (not_6_out, A_2);
  nand nand_1 (nand_1_out, A, not_1_out);
  nand nand_2 (nand_2_out, not_2_out, C);
  nand nand_3 (nand_3_out, not_3_out, B);
  not not_7 (not_7_out, C);
  nand nand_4 (nand_4_out, A_2, not_4_out);
  nand nand_5 (nand_5_out, not_5_out, C_2);
  nand nand_6 (nand_6_out, not_6_out, B_2);
  not not_8 (not_8_out, C_2);
  not not_9 (not_9_out, nand_1_out);
  not not_10 (not_10_out, not_9_out);
  not not_11 (not_11_out, not_12_out);
  not not_12 (not_12_out, nand_2_out);
  not not_13 (not_13_out, nand_3_out);
  not not_14 (not_14_out, nand_6_out);
  nand nand_7 (nand_7_out, not_13_out, not_7_out);
  nand nand_8 (nand_8_out, not_14_out, not_8_out);
  nand nand_9 (nand_9_out, not_10_out, not_11_out);
  not not_15 (not_15_out, nand_9_out);
  not not_16 (not_16_out, not_17_out);
  not not_17 (not_17_out, nand_7_out);
  nand nand_10 (nand_10_out, nand_4_out, nand_5_out);
  not not_18 (not_18_out, nand_10_out);
  nand nand_11 (nand_11_out, not_15_out, not_16_out);
  nand nand_12 (nand_12_out, not_18_out, nand_8_out);

  // Notes on the sheet:
  //   AB'
  //   A'C
  //   A'BC'
  //   AB'
  //   A'C
  //   A'BC'
  //   AB'+A'C
  //   AB'+A'C
  //   FIRST GO
  //   REWRITEN
  //   AB'+A'C+A'BC'
  //   AB'+A'C+A'BC'
endmodule
