// Logisim project lab2.3b.circ as structural Verilog: 1 circuit, main circuit main
module main (
  input  A,
  input  B,
  input  C,
  input  A_2,
  input  B_2,
  input  C_2
);

  wire nand_1_out, nand_2_out, nand_3_out, nand_4_out, nand_5_out, nand_6_out, not_1_out, not_2_out,
       not_3_out, not_4_out, not_5_out, not_6_out, not_7_out, not_8_out;

  not not_1 (not_1_out, B);
  not not_2 (not_2_out, A);
  not not_3 (not_3_out, A);
  not not_4 (not_4_out, not_1_out);
  not not_5 (not_5_out, not_2_out);
  not not_6 (not_6_out, C);
  not not_7 (not_7_out, A_2);
  not not_8 (not_8_out, C_2);
  nand nand_1 (nand_1_out, not_3_out, not_4_out);
  nand nand_2 (nand_2_out, not_5_out, not_6_out);
  nand nand_3 (nand_3_out, not_7_out, B_2);
  nand nand_4 (nand_4_out, A_2, not_8_out);
  nand nand_5 (nand_5_out, nand_1_out, nand_2_out);
  nand nand_6 (nand_6_out, nand_3_out, nand_4_out);
  // NOT_Gate not_9 has open pins: in=nand_5_out, out=open
  // NOT_Gate not_10 has open pins: in=nand_6_out, out=open

  // Notes on the sheet:
  //   (A + B')
  //   (A' + C)
  //   (A + B')
  //   (A' + C)
  //   FIRST GO
  //   (A + B')(A' + C)
  //   REWRITE
  //   (A + B')(A' + C)
endmodule
