// Logisim project lab2.4a.circ as structural Verilog: 1 circuit, main circuit main
module main (
  input  A,
  input  B,
  input  C,
  input  A_2,
  input  B_2,
  input  C_2
);

  wire nor_1_out, nor_2_out, nor_3_out, nor_4_out, nor_5_out, nor_6_out, not_1_out, not_2_out, not_3_out,
       not_4_out, not_5_out, not_6_out;

  not not_1 (not_1_out, B);
  not not_2 (not_2_out, B_2);
  nor nor_1 (nor_1_out, A, not_1_out);
  not not_3 (not_3_out, nor_1_out);
  not not_4 (not_4_out, nor_2_out);
  nor nor_2 (nor_2_out, A, C);
  nor nor_3 (nor_3_out, A_2, not_2_out);
  nor nor_4 (nor_4_out, A_2, C_2);
  not not_5 (not_5_out, not_3_out);
  not not_6 (not_6_out, not_4_out);
  nor nor_5 (nor_5_out, nor_3_out, nor_4_out);
  nor nor_6 (nor_6_out, not_5_out, not_6_out);

  // Notes on the sheet:
  //   (A + B')
  //   (A + C)
  //   (A + B')
  //   (A + C)
  //   FIRST GO
  //   (A + C)(A + B')
  //   REWRITE
  //   (A + C)(A + B')
endmodule
