// Logisim project lab2.4b.circ as structural Verilog: 1 circuit, main circuit main
module main (
  input  A,
  input  B,
  input  C,
  input  A_2,
  input  B_2,
  input  C_2
);

  wire nor_1_out, nor_2_out, nor_3_out, nor_4_out, nor_5_out, nor_6_out, not_1_out, not_2_out, not_3_out,
       not_4_out, not_5_out, not_6_out, not_7_out, not_8_out, not_9_out, not_10_out;

  not not_1 (not_1_out, A);
  not not_2 (not_2_out, not_3_out);
  not not_3 (not_3_out, B);
  not not_4 (not_4_out, B);
  not not_5 (not_5_out, C);
  not not_6 (not_6_out, not_5_out);
  not not_7 (not_7_out, A_2);
  not not_8 (not_8_out, B_2);
  nor nor_1 (nor_1_out, not_7_out, B_2);
  nor nor_2 (nor_2_out, not_8_out, C_2);
  nor nor_3 (nor_3_out, not_1_out, not_2_out);
  nor nor_4 (nor_4_out, not_4_out, not_6_out);
  nor nor_5 (nor_5_out, nor_1_out, nor_2_out);
  nor nor_6 (nor_6_out, nor_3_out, nor_4_out);
  not not_9 (not_9_out, nor_5_out);
  not not_10 (not_10_out, nor_6_out);

  // Notes on the sheet:
  //   BC'
  //   AB'
  //   BC'
  //   AB'
  //   REWRITE
  //   AB" + BC'
  //   FIRST GO
  //   AB" + BC'
endmodule
