// Logisim project lab2.5.circ as structural Verilog: 1 circuit, main circuit main
module main (
  input  x1,
  input  x2,
  input  x3
);

  wire and_1_out, and_2_out, not_1_out, or_1_out;

  not not_1 (not_1_out, x1);
  and and_1 (and_1_out, not_1_out, x2);
  and and_2 (and_2_out, x1, x3);
  or or_1 (or_1_out, and_1_out, and_2_out);

  // Notes on the sheet:
  //   X1' X2
  //   X1 X3
  //   X1 X3 + X1' X2
endmodule
