// Logisim project lab2.add3a.circ as structural Verilog: 1 circuit, main circuit main
module main (
  input  A,
  input  B,
  input  C,
  input  A_2,
  input  B_2,
  input  C_2
);

  wire and_1_out, and_2_out, nand_1_out, nand_2_out, nand_3_out, nand_4_out, not_1_out, not_2_out, not_3_out,
       not_4_out, not_5_out, not_6_out, not_7_out, not_8_out, not_9_out, not_10_out, not_11_out, not_12_out,
       or_1_out, or_2_out;

  not not_1 (not_1_out, A_2);
  not not_2 (not_2_out, B_2);
  not not_3 (not_3_out, B);
  not not_4 (not_4_out, not_2_out);
  or or_1 (or_1_out, A, not_3_out);
  nand nand_1 (nand_1_out, not_1_out, not_4_out);
  not not_5 (not_5_out, A_2);
  not not_6 (not_6_out, C_2);
  and and_1 (and_1_out, or_1_out, C);
  not not_7 (not_7_out, A);
  and and_2 (and_2_out, not_7_out, B, not_8_out);
  not not_8 (not_8_out, C);
  nand nand_2 (nand_2_out, nand_1_out, C_2);
  nand nand_3 (nand_3_out, not_5_out, B_2, not_6_out);
  not not_9 (not_9_out, nand_2_out);
  not not_10 (not_10_out, nand_3_out);
  or or_2 (or_2_out, and_1_out, and_2_out);
  not not_11 (not_11_out, not_9_out);
  not not_12 (not_12_out, not_10_out);
  nand nand_4 (nand_4_out, not_11_out, not_12_out);

  // Notes on the sheet:
  //   (A + B')C + A'BC', AND/OR/NOT
  //   (A + B')
  //   (A + B')C + A'BC', NAND and NOT
  //   (A + B')
  //   A'BC'
  //   (A + B')C
  //   (A + B')C
  //   A'BC'
  //   (A + B')C + A'BC'
  //   (A + B')C + A'BC'
endmodule
