// Logisim project lab2.add4Parity.circ as structural Verilog: 1 circuit, main circuit main
module main (
  input  A,
  input  B,
  input  C
);

  wire xor_1_out, xor_2_out;

  xor xor_1 (xor_1_out, A, B);
  xor xor_2 (xor_2_out, xor_1_out, C);

  // Notes on the sheet:
  //   Creating the Parity Bit for 3 Inputs
endmodule
